// Logisim project circuito_completo_alu.circ as structural Verilog: 6 circuits, main circuit main
module main (
  input  [1:0] op,
  input  a0,
  input  a1,
  input  a2,
  input  a3,
  input  b0,
  input  b1,
  input  b2,
  input  b3,
  output [7:0] out_10,
  output [3:0] out_11,
  output [3:0] out_12
);

  wire [6:0] rom_1_data, rom_2_data;
  wire [7:0] divider4bits_1_q, multiplicator_1_result, sum_sub_1_result, sum_sub_2_result;

  Multiplexer #(.select(2), .width(8)) multiplexer_1 (
    .in0(sum_sub_1_result), .in1(sum_sub_2_result), .in2(multiplicator_1_result), .in3(divider4bits_1_q),
    .out(out_10), .sel(op));
  ROM #(.addrWidth(4), .dataWidth(7)) rom_1 (.addr(out_10[7:4]), .data(rom_1_data));
  Hex_Digit_Display hex_digit_display_1 (.value(out_10[7:4]));  // open: dp
  _7_Segment_Display u_7_segment_display_1 (
    .g(rom_1_data[0]), .f(rom_1_data[1]), .a(rom_1_data[6]), .b(rom_1_data[5]), .e(rom_1_data[2]),
    .d(rom_1_data[3]), .c(rom_1_data[4]));  // open: dp
  Hex_Digit_Display hex_digit_display_2 (.value(out_10[3:0]));  // open: dp
  ROM #(.addrWidth(4), .dataWidth(7)) rom_2 (.addr(out_10[3:0]), .data(rom_2_data));
  _7_Segment_Display u_7_segment_display_2 (
    .g(rom_2_data[0]), .f(rom_2_data[1]), .a(rom_2_data[6]), .b(rom_2_data[5]), .e(rom_2_data[2]),
    .d(rom_2_data[3]), .c(rom_2_data[4]));  // open: dp
  sum_sub sum_sub_1 (.SUB(1'b0), .A({a3, a2, a1, a0}), .B({b3, b2, b1, b0}), .Result(sum_sub_1_result));  // open: Bout
  sum_sub sum_sub_2 (.SUB(1'b1), .A({a3, a2, a1, a0}), .B({b3, b2, b1, b0}), .Result(sum_sub_2_result));  // open: Bout
  multiplicator multiplicator_1 (.A({a3, a2, a1, a0}), .B({b3, b2, b1, b0}), .Result(multiplicator_1_result));
  Divider4bits divider4bits_1 (.A({a3, a2, a1, a0}), .B({b3, b2, b1, b0}), .Q(divider4bits_1_q));  // open: R

  assign out_11 = out_10[7:4];
  assign out_12 = out_10[3:0];

  // Notes on the sheet:
  //   s0 = 00 = soma
  //   s1 = 01 = sub
  //   s2 = 10 = multiplicacao
  //   s3 = 11 = div
  //   contents of rom_1 (hex, n*v repeats v):
  //   7e 30 6d 79 33 5b 5f 70 7f 7b 77 1f 4e 3d 4f 47
  //   contents of rom_2 (hex, n*v repeats v):
  //   7e 30 6d 79 33 5b 5f 70 7f 7b 77 1f 4e 3d 4f 47
  //   0 = soma
  //   1 = subtracao
endmodule

module sum_sub (
  input  SUB,
  input  [3:0] A,
  input  [3:0] B,
  output [7:0] Result,
  output Bout
);

  wire fulladder_1_carry_out, fulladder_2_carry_out, fulladder_3_carry_out, fulladder_4_carry_out, not_1_out,
       xor_1_out, xor_2_out, xor_3_out, xor_4_out;

  xor xor_1 (xor_1_out, B[0], SUB);
  xor xor_2 (xor_2_out, B[1], SUB);
  xor xor_3 (xor_3_out, B[2], SUB);
  xor xor_4 (xor_4_out, B[3], SUB);
  FULLADDER fulladder_1 (.a(A[0]), .b(xor_1_out), .carry_in(SUB), .soma(Result[0]), .carry_out(fulladder_1_carry_out));
  FULLADDER fulladder_2 (
    .a(A[1]), .b(xor_2_out), .carry_in(fulladder_1_carry_out), .soma(Result[1]),
    .carry_out(fulladder_2_carry_out));
  FULLADDER fulladder_3 (
    .a(A[2]), .b(xor_3_out), .carry_in(fulladder_2_carry_out), .soma(Result[2]),
    .carry_out(fulladder_3_carry_out));
  FULLADDER fulladder_4 (
    .a(A[3]), .b(xor_4_out), .carry_in(fulladder_3_carry_out), .soma(Result[3]),
    .carry_out(fulladder_4_carry_out));
  not not_1 (not_1_out, SUB);
  and and_1 (Bout, not_1_out, fulladder_4_carry_out);

  assign Result[7:4] = {3'b000, Bout};
endmodule

module multiplicator (
  input  [3:0] A,
  input  [3:0] B,
  output [7:0] Result
);

  wire [3:0] a0b0_out;
  wire [4:1] a0b1_out;
  wire [5:2] a0b2_out;
  wire [6:3] a0b3_out;
  wire [7:0] adder_1_out, adder_2_out;

  and a0b0 (a0b0_out[0], A[0], B[0]);
  and a1b0 (a0b0_out[1], A[1], B[0]);
  and a2b0 (a0b0_out[2], A[2], B[0]);
  and a3b0 (a0b0_out[3], A[3], B[0]);
  and a0b1 (a0b1_out[1], A[0], B[1]);
  and a1b1 (a0b1_out[2], A[1], B[1]);
  and a2b1 (a0b1_out[3], A[2], B[1]);
  and a3b1 (a0b1_out[4], A[3], B[1]);
  and a0b2 (a0b2_out[2], A[0], B[2]);
  and a1b2 (a0b2_out[3], A[1], B[2]);
  and a2b2 (a0b2_out[4], A[2], B[2]);
  and a3b2 (a0b2_out[5], A[3], B[2]);
  and a0b3 (a0b3_out[3], A[0], B[3]);
  and a1b3 (a0b3_out[4], A[1], B[3]);
  and a2b3 (a0b3_out[5], A[2], B[3]);
  and a3b3 (a0b3_out[6], A[3], B[3]);
  Adder adder_1 (.a({3'b000, a0b1_out, 1'b0}), .b({4'b0000, a0b0_out}), .out(adder_1_out));  // open: cin, cout
  Adder adder_2 (.a({2'b00, a0b2_out, 2'b00}), .b(adder_1_out), .out(adder_2_out));  // open: cin, cout
  Adder adder_3 (.a({1'b0, a0b3_out, 3'b000}), .b(adder_2_out), .out(Result));  // open: cin, cout
endmodule

module FULLADDER (
  input  a,
  input  b,
  input  carry_in,
  output soma,
  output carry_out
);

  wire and_1_out, and_2_out, and_3_out, xor_1_out;

  xor xor_1 (xor_1_out, a, b);
  and and_1 (and_1_out, a, carry_in);
  and and_2 (and_2_out, a, b);
  and and_3 (and_3_out, b, carry_in);
  or or_1 (carry_out, and_1_out, and_2_out, and_3_out);
  xor xor_2 (soma, xor_1_out, carry_in);
endmodule

module Divider4bits (
  input  [3:0] A,
  input  [3:0] B,
  output [3:0] R,
  output [7:0] Q
);

  wire [3:0] EST1_r_out, EST2_r_out, EST3_r_out;

  DividerState EST3 (.R_in(4'b0000), .A_i(A[3]), .B(B), .R_out(EST3_r_out), .Q(Q[3]));
  DividerState EST2 (.R_in(EST3_r_out), .A_i(A[2]), .B(B), .R_out(EST2_r_out), .Q(Q[2]));
  DividerState EST1 (.R_in(EST2_r_out), .A_i(A[1]), .B(B), .R_out(EST1_r_out), .Q(Q[1]));
  DividerState EST0 (.R_in(EST1_r_out), .A_i(A[0]), .B(B), .R_out(R), .Q(Q[0]));

  assign Q[7:4] = 4'b0000;
endmodule

module DividerState (
  input  [3:0] R_in,
  input  A_i,
  input  [3:0] B,
  output [3:0] R_out,
  output Q
);

  wire [3:0] adder_1_out, xor_1_out;

  assign xor_1_out = B ^ 4'b1111;  // XOR_Gate xor_1, 4 bits wide
  Adder #(.width(4)) adder_1 (.a({R_in[2:0], A_i}), .b(xor_1_out), .out(adder_1_out), .cin(1'b1), .cout(Q));
  Multiplexer #(.width(4)) multiplexer_1 (.in0({R_in[2:0], A_i}), .in1(adder_1_out), .out(R_out), .sel(Q));
endmodule
