// Logisim project circuito_somador_subtrator.circ as structural Verilog: 2 circuits, main circuit main
module main (
  input  sub,
  input  a0,
  input  a1,
  input  a2,
  input  a3,
  input  b0,
  input  b1,
  input  b2,
  input  b3,
  output out_10,
  output out_11,
  output out_12,
  output out_13,
  output out_14
);

  wire full_adder_1_cout, full_adder_2_cout, full_adder_3_cout, xor_1_out, xor_2_out, xor_3_out, xor_4_out;

  xor xor_1 (xor_1_out, sub, b0);
  xor xor_2 (xor_2_out, sub, b1);
  xor xor_3 (xor_3_out, sub, b2);
  xor xor_4 (xor_4_out, sub, b3);
  full_adder full_adder_1 (.a(a0), .b(xor_1_out), .cin(sub), .S(out_10), .Cout(full_adder_1_cout));
  full_adder full_adder_2 (.a(a1), .b(xor_2_out), .cin(full_adder_1_cout), .S(out_11), .Cout(full_adder_2_cout));
  full_adder full_adder_3 (.a(a2), .b(xor_3_out), .cin(full_adder_2_cout), .S(out_12), .Cout(full_adder_3_cout));
  full_adder full_adder_4 (.a(a3), .b(xor_4_out), .cin(full_adder_3_cout), .S(out_13), .Cout(out_14));
endmodule

module full_adder (
  input  a,
  input  b,
  input  cin,
  output S,
  output Cout
);

  wire and_1_out, and_2_out, xor_1_out;

  xor xor_1 (xor_1_out, a, b);
  and and_1 (and_1_out, a, b);
  and and_2 (and_2_out, xor_1_out, cin);
  xor xor_2 (S, xor_1_out, cin);
  or or_1 (Cout, and_1_out, and_2_out);
endmodule
