// Logisim project projeto_final_circuitos.circ as structural Verilog: 3 circuits, main circuit main
module main (
  input  sum,
  input  a0,
  input  a1,
  input  a2,
  input  a3,
  input  b0,
  input  b1,
  input  b2,
  input  b3,
  output [7:0] out_10
);

  wire fulladder_2_carry_out, fulladder_3_carry_out, fulladder_4_carry_out, xor_1_out, xor_2_out, xor_3_out,
       xor_4_out;
  wire [3:0] a0b0_out;
  wire [4:1] a0b1_out;
  wire [5:2] a0b2_out;
  wire [6:3] a0b3_out;
  wire [7:0] adder_1_out, adder_2_out;

  and a0b0 (a0b0_out[0], b0, a0);
  and a0b1 (a0b1_out[1], b1, a0);
  and a0b2 (a0b2_out[2], b2, a0);
  and a0b3 (a0b3_out[3], b3, a0);
  and a1b0 (a0b0_out[1], b0, a1);
  and a1b1 (a0b1_out[2], b1, a0);
  and a1b2 (a0b2_out[3], b2, a0);
  and a1b3 (a0b3_out[4], b3, a0);
  xor xor_1 (xor_1_out, b0, sum);
  xor xor_2 (xor_2_out, b1, sum);
  xor xor_3 (xor_3_out, b2, sum);
  xor xor_4 (xor_4_out, b3, sum);
  and a2b0 (a0b0_out[2], b0, a2);
  and a2b1 (a0b1_out[3], b1, a0);
  and a2b2 (a0b2_out[4], b2, a0);
  and a2b3 (a0b3_out[5], b3, a0);
  and a3b0 (a0b0_out[3], b0, a3);
  and a3b1 (a0b1_out[4], b1, a0);
  and a3b2 (a0b2_out[5], b2, a0);
  and a3b3 (a0b3_out[6], b3, a0);
  FULLADDER fulladder_1 (.a(a0), .b(xor_1_out), .carry_in(fulladder_2_carry_out));  // open: soma, carry_out
  FULLADDER fulladder_2 (
    .a(a1), .b(xor_2_out), .carry_in(fulladder_3_carry_out), .carry_out(fulladder_2_carry_out));  // open: soma
  Adder adder_1 (.a({3'b000, a0b1_out, 1'b0}), .b({4'b0000, a0b0_out}), .out(adder_1_out), .cin(1'b0));  // open: cout
  FULLADDER fulladder_3 (
    .a(a2), .b(xor_3_out), .carry_in(fulladder_4_carry_out), .carry_out(fulladder_3_carry_out));  // open: soma
  Adder adder_2 (.a({2'b00, a0b2_out, 2'b00}), .b(adder_1_out), .out(adder_2_out), .cin(1'b0));  // open: cout
  Adder adder_3 (.a({1'b0, a0b3_out, 3'b000}), .b(adder_2_out), .out(out_10), .cin(1'b0));  // open: cout
  Multiplexer #(.select(2), .width(8)) multiplexer_1 ();  // open: in0, in1, in2, in3, out, sel
  FULLADDER fulladder_4 (.a(a3), .b(xor_4_out), .carry_out(fulladder_4_carry_out));  // open: carry_in, soma
endmodule

module FULLADDER (
  input  a,
  input  b,
  input  carry_in,
  output soma,
  output carry_out
);

  wire and_1_out, and_2_out, and_3_out;

  xor xor_1 (soma, a, b);
  and and_1 (and_1_out, a, carry_in);
  and and_2 (and_2_out, a, b);
  and and_3 (and_3_out, b, carry_in);
  or or_1 (carry_out, and_1_out, and_2_out, and_3_out);
endmodule

module FA (
  input  a,
  input  b,
  output soma,
  output carry_out
);

  xor xor_1 (soma, a, b);
  and and_1 (carry_out, b, a);
endmodule
